# Fritzing sketch Schema_cablage_Fritzing (saved by Fritzing 0.9.3b)
breadboards: 1

parts:
  L2 = Solenoid
  WeMos_D1_Mini_Relay_Shield_V8 = WeMos D1 Mini Relay Shield V2
  L5 = Solenoid
  L7 = Solenoid
  L8 = Solenoid
  M3 = fc-51 [package=THT]
  S1 = SPST Switch [package=switch-spdt_kit]  # not connected
  Composant2 = ws2812b [package="smd 2812b"]
  Composant3 = ws2812b [package="smd 2812b"]
  Composant4 = ws2812b [package="smd 2812b"]
  Composant5 = ws2812b [package="smd 2812b"]
  Composant6 = ws2812b [package="smd 2812b"]
  Composant7 = ws2812b [package="smd 2812b"]
  Composant8 = ws2812b [package="smd 2812b"]
  Composant9 = ws2812b [package="smd 2812b"]
  M4 = fc-51 [package=THT]
  M5 = fc-51 [package=THT]
  M6 = fc-51 [package=THT]
  S2 = SPST Switch [package=switch-spdt_kit]
  S3 = SPST Switch [package=switch-spdt_kit]  # not connected
  S4 = SPST Switch [package=switch-spdt_kit]
  J1 = Piezo Speaker
  Composant10 = DeuLigne 1.1 - The Snootlab's LCD shield for Arduino
  Power_plug1 = Power plug
  S5 = Round Pushbutton
  S6 = Round Pushbutton
  M8 = fc-51 [package=THT]
  Composant1 = Arduino Mega 2560 (Rev3)
  L3 = Solenoid
  DC1 = DC_DC_XL4016 [package=board_screw]
  L9 = Solenoid
  L6 = Solenoid
  L4 = Solenoid
  WeMos_D1_Mini_Relay_Shield_V9 = WeMos D1 Mini Relay Shield V2
  WeMos_D1_Mini_Relay_Shield_V10 = WeMos D1 Mini Relay Shield V2
  WeMos_D1_Mini_Relay_Shield_V11 = WeMos D1 Mini Relay Shield V2
  WeMos_D1_Mini_Relay_Shield_V12 = WeMos D1 Mini Relay Shield V2
  WeMos_D1_Mini_Relay_Shield_V13 = WeMos D1 Mini Relay Shield V2
  WeMos_D1_Mini_Relay_Shield_V14 = WeMos D1 Mini Relay Shield V2
  WeMos_D1_Mini_Relay_Shield_V15 = WeMos D1 Mini Relay Shield V2
  M9 = fc-51 [package=THT]
  M10 = fc-51 [package=THT]
  M11 = fc-51 [package=THT]
  J5 = Wago 350 6 terminals [part_number="wago 350-6" package=THT]
  J6 = Wago 350 6 terminals [part_number="wago 350-6" package=THT]

nets:
  N1: L2.pin1, J5.pin3
  N2: L2.pin2, WeMos_D1_Mini_Relay_Shield_V11.NO
  N3: WeMos_D1_Mini_Relay_Shield_V8.COM, Power_plug1.VCC, DC1.IN+, WeMos_D1_Mini_Relay_Shield_V9.COM, WeMos_D1_Mini_Relay_Shield_V10.COM, WeMos_D1_Mini_Relay_Shield_V11.COM, WeMos_D1_Mini_Relay_Shield_V12.COM, WeMos_D1_Mini_Relay_Shield_V13.COM, WeMos_D1_Mini_Relay_Shield_V14.COM, WeMos_D1_Mini_Relay_Shield_V15.COM
  N4: L5.pin2, WeMos_D1_Mini_Relay_Shield_V14.NO
  N5: L7.pin2, WeMos_D1_Mini_Relay_Shield_V15.NO
  N6: L8.pin1, J6.pin6
  N7: L8.pin2, WeMos_D1_Mini_Relay_Shield_V12.NO
  N8: M3.pin1, Composant1.D7_PWM
  VDD: Composant2.VDD, Composant3.VDD, Composant4.VDD, Composant5.VDD, Composant6.VDD, Composant7.VDD, Composant8.VDD, Composant9.VDD
  VSS: Composant2.VSS, Composant3.VSS, Composant4.VSS, Composant5.VSS, Composant6.VSS, Composant7.VSS, Composant8.VSS, Composant9.VSS
  N9: Composant2.DIN, Composant3.DIN, Composant4.DIN, Composant5.DIN, Composant6.DIN, Composant7.DIN, Composant8.DIN
  N10: Composant9.DIN, Composant1.D13_PWM
  N11: M4.pin1, Composant1.D3_PWM
  N12: M5.pin1, Composant1.D4_PWM
  N13: M6.pin1, Composant1.D2_PWM
  N14: S2.O, Composant1.A0
  N15: S4.S, Composant1.A1
  N16: J1.pin2, Composant1.D10_PWM
  N17: Composant10.A0, Composant1.D21/SCL
  N18: Composant10.A1, Composant1.D20/SDA
  N19: Power_plug1.GND, DC1.IN-, J5.pin1
  N20: S5.leg1, WeMos_D1_Mini_Relay_Shield_V12.D1
  N21: S6.leg0, WeMos_D1_Mini_Relay_Shield_V12.D2
  N22: M8.pin1, Composant1.D5_PWM
  N23: Composant1.D9_PWM, M9.pin1
  N24: Composant1.D8_PWM, M10.pin1
  N25: Composant1.D6_PWM, M11.pin1
  N26: Composant1.D42, WeMos_D1_Mini_Relay_Shield_V12.D3
  N27: Composant1.D44, WeMos_D1_Mini_Relay_Shield_V9.D0
  N28: Composant1.D46, WeMos_D1_Mini_Relay_Shield_V9.D5
  N29: Composant1.D48, WeMos_D1_Mini_Relay_Shield_V12.D4
  N30: Composant1.D50, WeMos_D1_Mini_Relay_Shield_V9.D6
  N31: Composant1.D52, WeMos_D1_Mini_Relay_Shield_V9.D7
  N32: L3.pin1, J5.pin4
  N33: L3.pin2, WeMos_D1_Mini_Relay_Shield_V10.NO
  N34: L9.pin1, J5.pin2
  N35: L6.pin2, WeMos_D1_Mini_Relay_Shield_V9.NO
  N36: L4.pin1, J6.pin2
  N37: J5.pin5, J6.pin1

custom parts:
  Wago 350 6 terminals: Terminal strip with operating push buttons, RM 3.5 mm, 6-pin
